# Fritzing sketch Untitled Sketch 2 (saved by Fritzing 0.9.3b)

parts:
  S1 = H-Bridge with L298N
  S2 = H-Bridge with L298N
  パーツ2 = Freaduino 1.8
  DC_Mot_Enc1 = DC Motor with two-phase hall-encoder [part_number=VT-E-G25A-06-177E]
  DC_Mot_Enc2 = DC Motor with two-phase hall-encoder [part_number=VT-E-G25A-06-177E]
  DC_Mot_Enc3 = DC Motor with two-phase hall-encoder [part_number=VT-E-G25A-06-177E]
  U1 = LIPO-2000mAh [package=lipo-2000]

nets:
  12V: S1.12V, S2.12V, U1.+
  GND: S1.GND, S2.GND, U1.-
  N1: S1.ENA, パーツ2.FD10
  N2: S1.IN1, パーツ2.FD9
  N3: S1.IN2, パーツ2.FD8
  N4: S1.IN3, パーツ2.FD7
  N5: S1.IN4, パーツ2.FD6
  N6: S1.ENB, パーツ2.FD5
  N7: S1.M1-01, DC_Mot_Enc2.pin1
  N8: S1.M1-02, DC_Mot_Enc2.pin2
  N9: S1.M2-01, DC_Mot_Enc1.pin2
  N10: S1.M2-02, DC_Mot_Enc1.pin1
  N11: S2.IN3, パーツ2.FD13
  N12: S2.IN4, パーツ2.FD12
  N13: S2.ENB, パーツ2.FD11
  N14: S2.M1-01, DC_Mot_Enc3.pin1
  N15: S2.M1-02, DC_Mot_Enc3.pin2
  N16: パーツ2.A4/SDA, DC_Mot_Enc3.pin5
  N17: パーツ2.A5/SCL, DC_Mot_Enc3.pin6
  N18: パーツ2.FA1, DC_Mot_Enc2.pin6
  N19: パーツ2.FA1+, DC_Mot_Enc1.pin3
  N20: パーツ2.FA1-, DC_Mot_Enc1.pin4
  N21: パーツ2.FA2, DC_Mot_Enc1.pin5
  N22: パーツ2.FA2+, DC_Mot_Enc3.pin3
  N23: パーツ2.FA2-, DC_Mot_Enc3.pin4
  N24: パーツ2.FA3, DC_Mot_Enc1.pin6
  N25: パーツ2.FA0, DC_Mot_Enc2.pin5
  N26: パーツ2.FA0+, DC_Mot_Enc2.pin3
  N27: パーツ2.FA0-, DC_Mot_Enc2.pin4

custom parts:
  H-Bridge with L298N: h-bridge
  Freaduino 1.8: Freaduino UNO is an Arduino compatible board. It is based on Arduino UNO Rev3 design. So you can use Freaduino as Arduino UNO Rev3 . All code, shield and IDE for Arduino UNO Rev3 are also valid on Freaduino UNO. Some visible improvement on hardware make Freaduino UNO more flexible and easier to use. For example: 3.3v or 5v IO selectable allow you connect some 3.3v modules (such as XBee) to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
